// Logisim project CPU.circ as structural Verilog: 6 circuits, main circuit main
module main (
  input  Clock
);

  wire ALU_n, ALU_z, and_1_out, and_2_out, and_3_out, and_4_out, and_5_out, and_6_out,
       Calc_Branch_take_branch, nor_1_out, not_1_out;
  wire [7:0] ALU_rd, multiplexer_1_out, multiplexer_2_out, ram_1_rd, RF_rs1, RF_rs2;
  wire [15:0] ROM_inst_15_0;

  nor nor_1 (nor_1_out, and_2_out, and_1_out);
  and and_1 (and_1_out, and_3_out, and_4_out);
  ROM ROM (
    .BRANCH_LABEL({{2{ROM_inst_15_0[11]}}, ROM_inst_15_0[10:5]}), .Clock(Clock),
    .TAKE_BRANCH(Calc_Branch_take_branch), .INST_15_0(ROM_inst_15_0));
  and and_2 (and_2_out, ROM_inst_15_0[0], ROM_inst_15_0[4]);
  and and_3 (and_3_out, ~ROM_inst_15_0[3], ~ROM_inst_15_0[4]);  // AND_Gate
  and and_4 (and_4_out, ROM_inst_15_0[1], ROM_inst_15_0[0], ROM_inst_15_0[2]);
  not not_1 (not_1_out, nor_1_out);
  and and_5 (and_5_out, ~ROM_inst_15_0[4], ~ROM_inst_15_0[3], ROM_inst_15_0[2], ~ROM_inst_15_0[1], ROM_inst_15_0[0]);  // AND_Gate
  RegFile RF (
    .SELECT_RS1(ROM_inst_15_0[13:12]), .Wen(nor_1_out), .SELECT_RD(ROM_inst_15_0[15:14]),
    .SELECT_RS2(ROM_inst_15_0[11:10]), .CLOCK(Clock), .RD_DATA(multiplexer_2_out), .Branch_Store(not_1_out),
    .RS1(RF_rs1), .RS2(RF_rs2));
  and and_6 (and_6_out, ~ROM_inst_15_0[4], ROM_inst_15_0[0]);  // AND_Gate
  Multiplexer #(.width(8), .enable("false")) multiplexer_1 (
    .in0(RF_rs2), .in1({{2{ROM_inst_15_0[11]}}, ROM_inst_15_0[10:5]}), .out(multiplexer_1_out),
    .sel(and_6_out));
  ALU ALU (.RS1(RF_rs1), .RS2_IMM(multiplexer_1_out), .OPCODE(ROM_inst_15_0[4:0]), .Rd(ALU_rd), .Z(ALU_z), .N(ALU_n));
  RAM ram_1 (.RS1(ALU_rd), .RS2(RF_rs2), .OPCODE(ROM_inst_15_0[4:0]), .Clock(Clock), .Rd(ram_1_rd));
  Calc_Branch Calc_Branch (.N(ALU_n), .Z(ALU_z), .OPCODE(ROM_inst_15_0[4:0]), .TAKE_BRANCH(Calc_Branch_take_branch));
  Multiplexer #(.width(8), .enable("false")) multiplexer_2 (
    .in0(ALU_rd), .in1(ram_1_rd), .out(multiplexer_2_out), .sel(and_5_out));
endmodule

module RegFile (
  input  [1:0] SELECT_RS1,
  input  Wen,
  input  [1:0] SELECT_RD,
  input  [1:0] SELECT_RS2,
  input  CLOCK,
  input  [7:0] RD_DATA,
  input  Branch_Store,
  output [7:0] RS1,
  output [7:0] RS2
);

  wire demultiplexer_1_out0, demultiplexer_1_out1, demultiplexer_1_out2, demultiplexer_1_out3;
  wire [1:0] multiplexer_1_out;
  wire [7:0] Reg0_q, Reg1_q, Reg2_q, Reg3_q;

  Demultiplexer #(.select(2), .enable("false")) demultiplexer_1 (
    .out0(demultiplexer_1_out0), .out1(demultiplexer_1_out1), .out2(demultiplexer_1_out2),
    .out3(demultiplexer_1_out3), .in(Wen), .sel(SELECT_RD));
  Register #(.trigger("falling")) Reg0 (.D(RD_DATA), .en(demultiplexer_1_out0), .Q(Reg0_q), .clk(CLOCK));  // open: clr
  Multiplexer #(.width(2), .enable("false")) multiplexer_1 (
    .in0(SELECT_RS2), .in1(SELECT_RD), .out(multiplexer_1_out), .sel(Branch_Store));
  Register #(.trigger("falling")) Reg1 (.D(RD_DATA), .en(demultiplexer_1_out1), .Q(Reg1_q), .clk(CLOCK));  // open: clr
  Register #(.trigger("falling")) Reg2 (.D(RD_DATA), .en(demultiplexer_1_out2), .Q(Reg2_q), .clk(CLOCK));  // open: clr
  Register #(.trigger("falling")) Reg3 (.D(RD_DATA), .en(demultiplexer_1_out3), .Q(Reg3_q), .clk(CLOCK));  // open: clr
  Multiplexer #(.select(2), .width(8), .enable("false")) multiplexer_2 (
    .in0(Reg0_q), .in1(Reg1_q), .in2(Reg2_q), .in3(Reg3_q), .out(RS1), .sel(SELECT_RS1));
  Multiplexer #(.select(2), .width(8), .enable("false")) multiplexer_3 (
    .in0(Reg0_q), .in1(Reg1_q), .in2(Reg2_q), .in3(Reg3_q), .out(RS2), .sel(multiplexer_1_out));
endmodule

module ROM (
  input  [7:0] BRANCH_LABEL,
  input  Clock,
  input  TAKE_BRANCH,
  output [15:0] INST_15_0
);

  wire [7:0] adder_1_out, multiplexer_1_out, PC_q;

  Multiplexer #(.width(8), .enable("false")) multiplexer_1 (
    .in0(8'h1), .in1(BRANCH_LABEL), .out(multiplexer_1_out), .sel(TAKE_BRANCH));
  Adder adder_1 (.a(PC_q), .b(multiplexer_1_out), .out(adder_1_out));  // open: cin, cout
  Counter PC (.load(Clock), .D(adder_1_out), .count(1'b0), .Q(PC_q), .clk(Clock));  // open: carry, clr
  ROM_part #(.dataWidth(16)) rom_1 (.addr(PC_q), .data(INST_15_0));  // open: sel

  // Notes on the sheet:
  //   contents of rom_1 (hex, n*v repeats v):
  //   0 18 5418 a818 fc18 a1 5000 4053 5061 5081 4087 8085
endmodule

module ALU (
  input  [7:0] RS1,
  input  [7:0] RS2_IMM,
  input  [4:0] OPCODE,
  output [7:0] Rd,
  output Z,
  output N
);

  wire [7:0] adder_1_out, and_1_out, or_1_out, subtractor_1_out, xor_1_out;

  Adder adder_1 (.a(RS1), .b(RS2_IMM), .out(adder_1_out));  // open: cin, cout
  Subtractor subtractor_1 (.a(RS1), .b(RS2_IMM), .out(subtractor_1_out));  // open: bin, bout
  assign and_1_out = RS1 & RS2_IMM;  // AND_Gate and_1, 8 bits wide
  assign or_1_out = RS1 | RS2_IMM;  // OR_Gate or_1, 8 bits wide
  assign xor_1_out = RS1 ^ RS2_IMM;  // XOR_Gate xor_1, 8 bits wide
  Multiplexer #(.select(5), .width(8), .enable("false")) multiplexer_1 (
    .in0(adder_1_out), .in1(adder_1_out), .in4(subtractor_1_out), .in5(adder_1_out), .in7(adder_1_out),
    .in16(and_1_out), .in19(subtractor_1_out), .in20(or_1_out), .in23(subtractor_1_out), .in24(xor_1_out),
    .in27(subtractor_1_out), .in31(subtractor_1_out), .out({N, Rd[6:0]}), .sel(OPCODE));  // open: in2, in3, in6, in8, in9, in10, in11, in12, in13, in14, in15, in17, in18, in21, in22, in25, in26, in28, in29, in30
  nor nor_1 (Z, Rd[0], Rd[1], Rd[2], Rd[3], Rd[4], Rd[5], Rd[6], N);

  assign Rd[7] = N;
endmodule

module RAM (
  input  [7:0] RS1,
  input  [7:0] RS2,
  input  Clock,
  input  [4:0] OPCODE,
  output [7:0] Rd
);

  wire and_1_out, and_2_out, and_3_out, and_4_out, and_5_out;

  and and_1 (and_1_out, OPCODE[0], OPCODE[1], OPCODE[2]);
  and and_2 (and_2_out, ~OPCODE[3], ~OPCODE[4]);  // AND_Gate
  and and_3 (and_3_out, OPCODE[0], ~OPCODE[1], OPCODE[2]);  // AND_Gate
  and and_4 (and_4_out, and_1_out, and_2_out);
  and and_5 (and_5_out, and_2_out, and_3_out);
  RAM_part #(.bus("separate")) ram_1 (
    .addr(RS1), .din(RS2), .data(Rd), .str(and_4_out), .sel(1'b1), .clk(Clock), .ld(and_5_out), .clr(1'b0));
endmodule

module Calc_Branch (
  input  N,
  input  Z,
  input  [4:0] OPCODE,
  output TAKE_BRANCH
);

  wire and_1_out, and_2_out, and_3_out, and_4_out, IF_BRANCH_out, not_1_out, or_1_out;

  and IF_BRANCH (IF_BRANCH_out, OPCODE[4], OPCODE[1], OPCODE[0]);
  and and_1 (and_1_out, IF_BRANCH_out, Z);
  not not_1 (not_1_out, Z);
  and and_2 (and_2_out, IF_BRANCH_out, not_1_out);
  and and_3 (and_3_out, IF_BRANCH_out, N);
  or or_1 (or_1_out, Z, N);
  and and_4 (and_4_out, IF_BRANCH_out, or_1_out);
  Multiplexer #(.select(2), .enable("false")) multiplexer_1 (
    .in0(and_1_out), .in1(and_2_out), .in2(and_3_out), .in3(and_4_out), .out(TAKE_BRANCH), .sel(OPCODE[3:2]));
endmodule
